# Fritzing sketch cleaning_robot (saved by Fritzing 0.9.6b)
breadboards: 1

parts:
  L298N1 = L298N DC motor driver
  M1 = DC Motor
  M2 = DC Motor
  J1 = STM32 Nucleo boards
  M3 = DC Motor
  R2 = Resistor [tolerance=±5% resistance=220 package="1206 [SMD]"]
  VCC1 = Battery block 9V
  J3 = Buzzer
  M4 = fc-51 [package=THT]

nets:
  N1: L298N1.OUT1, M2.pin_2
  N2: L298N1.OUT2, M2.pin_1
  N3: L298N1.OUT3, M1.pin_2
  N4: L298N1.OUT4, M1.pin_1
  N5: L298N1.12V, VCC1.+
  N6: L298N1.GND, J1.GND#1188, R2.Pin_0, VCC1.-, J3.pin1, M4.pin2
  N7: L298N1.5V, J1.E5V
  N8: L298N1.ENA, J1.A0
  N9: L298N1.ENB, J1.A1
  N10: L298N1.IN1, J1.PC0
  N11: L298N1.IN2, J1.PC1
  N12: L298N1.IN3, J1.PC2
  N13: L298N1.IN4, J1.PC3
  N14: J1.PA12, J3.pin2
  N15: J1.IDD_01, J1.IDD_02
  N16: J1.CN_01, J1.CN_02
  N17: J1.CN_03, J1.CN_04
  N18: J1.JP5_2, J1.JP5_03
  N19: J1.GND#880, J1.GND#881
  N20: J1.GND#1149, J1.GND#1150
  N21: J1.3V3, M4.pin3
  N22: J1.PA9, M4.pin1
  N23: J1.PA10, M3.pin_1
  N24: M3.pin_2, R2.Pin_1

notes:
  vacuum
  cable from battery and l298n should be connected directly together and eventually to the breadboard (put the 3 cable in an electrical clamp)
  10Ohm
  if the voltage is too low, we can use a transistor with a higher voltage supply. the output pin will be connected to the middle pin in the transistor

custom parts:
  L298N DC motor driver: 2x DC motor driver with 78M05 positive voltage regulator (7..35 V) L298N: max 46 V, 2 A Set 5 V Enable jumper to enable 5 V regultor (needed for the L298N) and +5 V output at screw terminal or supply external +5 V at screw terminal Set ENA and/or ENB to +5 V to enable motor permanently or supply ENA and/or ENB with PWM signal IN1 and IN2 set rotation directory for motor A (OUT1/OUT2) IN2 and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
  Buzzer: Fixed frequency buzzer
